# Fritzing sketch HAT Fritzing template (saved by Fritzing 0.9.1b)
breadboards: 1

parts:
  part = female pin header, 2 pins [form="♀ (female)"]
  Raspberry_Pi1 = Raspberry Pi B+
  part_2 = Resistor [tolerance=±5% resistance=3.9k package=THT]
  part_3 = Resistor [tolerance=±5% resistance=3.9k package=THT]
  IC1 = 24LC32 [package=THT]
  C5 = Capacitor [part_number=10nF package=cap-pth-5mm]
  R3 = Resistor [tolerance=±5% resistance=1k package=THT]

nets:
  N1: part.pin1, IC1.WP_-_Write_Protect, R3.Pin_1
  GND: part.pin2, Raspberry_Pi1.GND, IC1.A0, IC1.A1, IC1.A2, IC1.0V, C5.1
  3.3V: Raspberry_Pi1.3V3, part_2.Pin_0, part_3.Pin_0, IC1.+V, C5.2, R3.Pin_0
  N2: Raspberry_Pi1.ID_SD, part_3.Pin_1, IC1.SDA_-_I2C_Data
  N3: Raspberry_Pi1.ID_SC, part_2.Pin_1, IC1.SCL_-_I2C_Clock
  5V: Raspberry_Pi1.5V

custom parts:
  Raspberry Pi B+: The awesome Raspberry Pi ARM Board with 40 pin gipo. Ready for special designed Raspberry Pi B+ Hat (Hardware attached (on) top)
